# Fritzing sketch Practica_1 (saved by Fritzing 0.9.3b)
breadboards: 1

parts:
  1_-_Blink = Arduino Uno (Rev3)
  LED1 = LED - 5mm [color="Red (633nm)" package="5 mm [THT]"]
  R1 = Resistor [tolerance=±5% resistance=220 package=THT]

nets:
  N1: 1_-_Blink.D12/MISO, LED1.anode
  N2: 1_-_Blink.GND, R1.Pin_1
  N3: LED1.cathode, R1.Pin_0
