# Fritzing sketch Practica_2 (saved by Fritzing 0.9.3b)
breadboards: 1

parts:
  Componente1 = Arduino Uno (Rev3)
  LED2 = LED - 5mm [color="Yellow (595nm)" package="5 mm [THT]"]
  R1 = Resistor [tolerance=±5% resistance=220 package=THT]
  LED1 = LED - 5mm [color="Red (633nm)" package="5 mm [THT]"]
  LED3 = LED - 5mm [color="Green (570nm)" package="5 mm [THT]"]
  R2 = Resistor [tolerance=±5% resistance=220 package=THT]
  R3 = Resistor [tolerance=±5% resistance=220 package=THT]

nets:
  N1: Componente1.D8, LED3.anode
  N2: Componente1.D10_PWM/SS, LED2.anode
  N3: Componente1.D12/MISO, LED1.anode
  N4: Componente1.GND, R1.Pin_1, R2.Pin_1, R3.Pin_1
  N5: LED2.cathode, R2.Pin_0
  N6: R1.Pin_0, LED1.cathode
  N7: LED3.cathode, R3.Pin_0
