# Fritzing sketch Practica_3 (saved by Fritzing 0.9.3b)
breadboards: 1

parts:
  R2 = Resistor [tolerance=±5% resistance=220 package=THT]
  LED1 = LED - 5mm [color="Red (633nm)" package="5 mm [THT]"]
  R1 = Resistor [tolerance=±5% resistance=10k package=THT]
  S1 = Pushbutton [package="[THT]"]
  3_-_Pulsador_e_Led = Arduino Uno (Rev3)

nets:
  N1: R2.Pin_0, LED1.cathode
  N2: R2.Pin_1, R1.Pin_1, 3_-_Pulsador_e_Led.GND
  N3: LED1.anode, 3_-_Pulsador_e_Led.D12/MISO
  N4: R1.Pin_0, S1.Pin_1, S1.Pin_2, 3_-_Pulsador_e_Led.D2
  N5: S1.Pin_3, S1.Pin_4, 3_-_Pulsador_e_Led.5V
