# Fritzing sketch Practica_4 (saved by Fritzing 0.9.3b)
breadboards: 1

parts:
  R2 = Resistor [tolerance=±5% resistance=220 package=THT]
  LED1 = LED - 5mm [color="White (4500K)" package="5 mm [THT]"]
  R3 = Resistor [tolerance=±5% resistance=10k package=THT]
  LDR = Arduino Uno (Rev3)
  R1 = Photocell (LDR) [package=THT]

nets:
  N1: R2.Pin_0, LED1.cathode
  N2: R2.Pin_1, R3.Pin_1, LDR.GND
  N3: LED1.anode, LDR.D12/MISO
  N4: R3.Pin_0, LDR.A0, R1.pin_1
  N5: LDR.5V, R1.pin_0
