# Fritzing sketch Practica_5 (saved by Fritzing 0.9.3b)
breadboards: 1

parts:
  R1 = Resistor [tolerance=±5% resistance=220 package=THT]
  LED1 = LED - 5mm [color="Red (633nm)" package="5 mm [THT]"]
  R2 = Rotary Potentiometer (Small) [maximum_resistance=10kΩ package=THT]
  5_Sinais_PWM = Arduino Uno (Rev3)

nets:
  N1: R1.Pin_0, R2.leg2, 5_Sinais_PWM.GND
  N2: R1.Pin_1, LED1.cathode
  N3: LED1.anode, 5_Sinais_PWM.D11_PWM/MOSI
  N4: R2.leg1, 5_Sinais_PWM.5V
  N5: R2.wiper, 5_Sinais_PWM.A0
