# Fritzing sketch Practica_6 (saved by Fritzing 0.9.3b)
breadboards: 1

parts:
  R2 = Resistor [tolerance=±5% resistance=220 package=THT]
  LED1 = LED - 5mm [color="Red (633nm)" package="5 mm [THT]"]
  R1 = Resistor [tolerance=±5% resistance=10k package=THT]
  S1 = Pushbutton [package="[THT]"]
  6_-_Bucles = Arduino Uno (Rev3)

nets:
  N1: R2.Pin_0, LED1.cathode
  N2: R2.Pin_1, R1.Pin_1, 6_-_Bucles.GND
  N3: LED1.anode, 6_-_Bucles.D12/MISO
  N4: R1.Pin_0, S1.Pin_1, S1.Pin_2, 6_-_Bucles.D2
  N5: S1.Pin_3, S1.Pin_4, 6_-_Bucles.5V
