# Fritzing sketch Practica_7 (saved by Fritzing 0.9.3b)
breadboards: 1

parts:
  7_-_Coche_fantástico = Arduino Uno (Rev3)
  R1 = Resistor [tolerance=±5% resistance=220 package=THT]
  R2 = Resistor [tolerance=±5% resistance=220 package=THT]
  R3 = Resistor [tolerance=±5% resistance=220 package=THT]
  R4 = Resistor [tolerance=±5% resistance=220 package=THT]
  R5 = Resistor [tolerance=±5% resistance=220 package=THT]
  LED2 = LED - 5mm [color="Red (633nm)" package="5 mm [THT]"]
  LED3 = LED - 5mm [color="Red (633nm)" package="5 mm [THT]"]
  LED4 = LED - 5mm [color="Red (633nm)" package="5 mm [THT]"]
  LED5 = LED - 5mm [color="Red (633nm)" package="5 mm [THT]"]
  LED1 = LED - 5mm [color="Red (633nm)" package="5 mm [THT]"]

nets:
  N1: 7_-_Coche_fantástico.D9_PWM, LED5.anode
  N2: 7_-_Coche_fantástico.D10_PWM/SS, LED4.anode
  N3: 7_-_Coche_fantástico.D11_PWM/MOSI, LED3.anode
  N4: 7_-_Coche_fantástico.D12/MISO, LED2.anode
  N5: 7_-_Coche_fantástico.D13/SCK, LED1.anode
  N6: 7_-_Coche_fantástico.GND, R1.Pin_0, R2.Pin_0, R3.Pin_0, R4.Pin_0, R5.Pin_0
  N7: R1.Pin_1, LED1.cathode
  N8: R2.Pin_1, LED2.cathode
  N9: R3.Pin_1, LED3.cathode
  N10: R4.Pin_1, LED4.cathode
  N11: R5.Pin_1, LED5.cathode
