# Fritzing sketch demo_domotica (saved by Fritzing 0.9.3b)
breadboards: 1

parts:
  Componente1 = Arduino Uno (Rev3)
  R1 = Photocell (LDR) [package=THT]
  J1 = Basic Servo
  R2 = Photocell (LDR) [package=THT]
  R3 = Photocell (LDR) [package=THT]
  R4 = Resistor [tolerance=±5% resistance=220 package=THT]
  R5 = Resistor [tolerance=±5% resistance=220 package=THT]
  R6 = Resistor [tolerance=±5% resistance=220 package=THT]

nets:
  N1: Componente1.A0, R1.pin_0
  N2: Componente1.A1, R2.pin_0
  N3: Componente1.A2, R3.pin_0
  N4: Componente1.D6_PWM, J1.pulse
  5V: Componente1.5V, J1.vcc, R4.Pin_0, R5.Pin_0, R6.Pin_0
  GND: Componente1.GND, J1.gnd
  N5: R1.pin_1, R4.Pin_1
  N6: R2.pin_1, R5.Pin_1
  N7: R3.pin_1, R6.Pin_1
